# Fritzing sketch piFoosball (saved by Fritzing 0.9.2b)
circuit board: 8.46667cm x 5.64444cm
breadboards: 1

parts:
  Cobbler = T Cobbler Plus
  Display_1 = 7 Segment Display
  Switch_2 = Momentary Switch [package=ksa_sealed_tac_switch]
  Switch_1 = Momentary Switch [package=ksa_sealed_tac_switch]

nets:
  N1: Cobbler.GND#19, Switch_2.4, Switch_1.4
  N2: Cobbler.SCLK, Cobbler.#5, Cobbler.#6, Cobbler.#19, Display_1.Segment_A, Display_1.Segment_F, Display_1.common_anode, Display_1.Segment_DP, Display_1.Segment_D, Display_1.Segment_B
  N3: Cobbler.#13, Display_1.Segment_E
  N4: Cobbler.GND#38, Switch_2.3
  N5: Cobbler.#21, Switch_1.3

custom parts:
  T Cobbler Plus: The T-Cobbler Plus is an add on prototyping board from Adafruit specifically designed for the Raspberry Pi B+ that can break out all those tasty power, GPIO, I2C and SPI pins from the 40-pin header onto a solderless breadboard. This set will make "cobbling together" prototypes with the Pi super easy. The T-Cobbler Plus can plug into any solderless breadboard.
